// Digital circuit 1_1Sram.dig as structural Verilog
module _1_1Sram (
  input  WD,
  input  WS,
  input  RS1,
  input  RS2,
  input  clk,
  output RD1,
  output RD2
);

  wire d_ff_1_q, multiplexer_1_out;

  Multiplexer multiplexer_1 (.sel(WS), .in_0(d_ff_1_q), .in_1(WD), .out(multiplexer_1_out));
  D_FF d_ff_1 (.D(multiplexer_1_out), .C(clk), .Q(d_ff_1_q));  // open: nQ
  and and_1 (RD1, d_ff_1_q, RS1);
  and and_2 (RD2, d_ff_1_q, RS2);

  // Notes on the sheet:
  //   clk: Hz: 2
endmodule
