// Digital circuit 1bit_adder.dig as structural Verilog
module _1bit_adder (
  input  X,
  input  Y,
  input  cin,
  output S,
  output Cout
);

  wire and_1_out, and_2_out, xor_1_out;

  and and_1 (and_1_out, X, Y);
  xor xor_1 (xor_1_out, X, Y);
  xor xor_2 (S, xor_1_out, cin);
  and and_2 (and_2_out, xor_1_out, cin);
  or or_1 (Cout, and_2_out, and_1_out);
endmodule
