// Digital circuit 1bit_reg.dig as structural Verilog
module _1bit_reg (
  input  din,
  input  sel,
  input  clk,
  output dout
);

  wire multiplexer_1_out;

  Multiplexer multiplexer_1 (.sel(sel), .in_0(dout), .in_1(din), .out(multiplexer_1_out));
  D_FF d_ff_1 (.D(multiplexer_1_out), .C(clk), .Q(dout));  // open: nQ

  // Notes on the sheet:
  //   clk: Hz: 2
endmodule
