// Digital circuit 1x17bit_ram.dig as structural Verilog
module _1x17bit_ram (
  input  RS1,
  input  RS2,
  input  WS,
  input  [16:0] WD_16_0,
  input  CLK,
  output [16:0] RD1_16_0,
  output [16:0] RD2_16_0
);

  _1_1Sram _1_1sram_1 (
    .WD(WD_16_0[16]), .WS(WS), .RS1(RS1), .RS2(RS2), .clk(CLK), .RD1(RD1_16_0[16]), .RD2(RD2_16_0[16]));
  _1_1Sram _1_1sram_2 (
    .WD(WD_16_0[11]), .WS(WS), .RS1(RS1), .RS2(RS2), .clk(CLK), .RD1(RD1_16_0[11]), .RD2(RD2_16_0[11]));
  _1_1Sram _1_1sram_3 (.WD(WD_16_0[6]), .WS(WS), .RS1(RS1), .RS2(RS2), .clk(CLK), .RD1(RD1_16_0[6]), .RD2(RD2_16_0[6]));
  _1_1Sram _1_1sram_4 (
    .WD(WD_16_0[15]), .WS(WS), .RS1(RS1), .RS2(RS2), .clk(CLK), .RD1(RD1_16_0[15]), .RD2(RD2_16_0[15]));
  _1_1Sram _1_1sram_5 (
    .WD(WD_16_0[10]), .WS(WS), .RS1(RS1), .RS2(RS2), .clk(CLK), .RD1(RD1_16_0[10]), .RD2(RD2_16_0[10]));
  _1_1Sram _1_1sram_6 (.WD(WD_16_0[5]), .WS(WS), .RS1(RS1), .RS2(RS2), .clk(CLK), .RD1(RD1_16_0[5]), .RD2(RD2_16_0[5]));
  _1_1Sram _1_1sram_7 (.WD(WD_16_0[1]), .WS(WS), .RS1(RS1), .RS2(RS2), .clk(CLK), .RD1(RD1_16_0[1]), .RD2(RD2_16_0[1]));
  _1_1Sram _1_1sram_8 (
    .WD(WD_16_0[14]), .WS(WS), .RS1(RS1), .RS2(RS2), .clk(CLK), .RD1(RD1_16_0[14]), .RD2(RD2_16_0[14]));
  _1_1Sram _1_1sram_9 (.WD(WD_16_0[9]), .WS(WS), .RS1(RS1), .RS2(RS2), .clk(CLK), .RD1(RD1_16_0[9]), .RD2(RD2_16_0[9]));
  _1_1Sram _1_1sram_10 (
    .WD(WD_16_0[4]), .WS(WS), .RS1(RS1), .RS2(RS2), .clk(CLK), .RD1(RD1_16_0[4]), .RD2(RD2_16_0[4]));
  _1_1Sram _1_1sram_11 (
    .WD(WD_16_0[0]), .WS(WS), .RS1(RS1), .RS2(RS2), .clk(CLK), .RD1(RD1_16_0[0]), .RD2(RD2_16_0[0]));
  _1_1Sram _1_1sram_12 (
    .WD(WD_16_0[13]), .WS(WS), .RS1(RS1), .RS2(RS2), .clk(CLK), .RD1(RD1_16_0[13]), .RD2(RD2_16_0[13]));
  _1_1Sram _1_1sram_13 (
    .WD(WD_16_0[8]), .WS(WS), .RS1(RS1), .RS2(RS2), .clk(CLK), .RD1(RD1_16_0[8]), .RD2(RD2_16_0[8]));
  _1_1Sram _1_1sram_14 (
    .WD(WD_16_0[3]), .WS(WS), .RS1(RS1), .RS2(RS2), .clk(CLK), .RD1(RD1_16_0[3]), .RD2(RD2_16_0[3]));
  _1_1Sram _1_1sram_15 (
    .WD(WD_16_0[12]), .WS(WS), .RS1(RS1), .RS2(RS2), .clk(CLK), .RD1(RD1_16_0[12]), .RD2(RD2_16_0[12]));
  _1_1Sram _1_1sram_16 (
    .WD(WD_16_0[7]), .WS(WS), .RS1(RS1), .RS2(RS2), .clk(CLK), .RD1(RD1_16_0[7]), .RD2(RD2_16_0[7]));
  _1_1Sram _1_1sram_17 (
    .WD(WD_16_0[2]), .WS(WS), .RS1(RS1), .RS2(RS2), .clk(CLK), .RD1(RD1_16_0[2]), .RD2(RD2_16_0[2]));

  // Other names for the same wires on the sheet: RD1_00 = RD1_16_0[0]; RD1_01 = RD1_16_0[1]; RD1_02 = RD1_16_0[2];
  //   RD1_03 = RD1_16_0[3]; RD1_04 = RD1_16_0[4]; RD1_05 = RD1_16_0[5]; RD1_06 = RD1_16_0[6]; RD1_07 = RD1_16_0[7];
  //   RD1_08 = RD1_16_0[8]; RD1_09 = RD1_16_0[9]; RD1_10 = RD1_16_0[10]; RD1_11 = RD1_16_0[11]; RD1_12 = RD1_16_0[12];
  //   RD1_13 = RD1_16_0[13]; RD1_14 = RD1_16_0[14]; RD1_15 = RD1_16_0[15]; RD1_16 = RD1_16_0[16];
  //   RD2_00 = RD2_16_0[0]; RD2_01 = RD2_16_0[1]; RD2_02 = RD2_16_0[2]; RD2_03 = RD2_16_0[3]; RD2_04 = RD2_16_0[4];
  //   RD2_05 = RD2_16_0[5]; RD2_06 = RD2_16_0[6]; RD2_07 = RD2_16_0[7]; RD2_08 = RD2_16_0[8]; RD2_09 = RD2_16_0[9];
  //   RD2_10 = RD2_16_0[10]; RD2_11 = RD2_16_0[11]; RD2_12 = RD2_16_0[12]; RD2_13 = RD2_16_0[13];
  //   RD2_14 = RD2_16_0[14]; RD2_15 = RD2_16_0[15]; RD2_16 = RD2_16_0[16]; WD0 = WD_16_0[0]; WD1 = WD_16_0[1];
  //   WD2 = WD_16_0[2]; WD3 = WD_16_0[3]; WD4 = WD_16_0[4]; WD5 = WD_16_0[5]; WD6 = WD_16_0[6]; WD7 = WD_16_0[7];
  //   WD8 = WD_16_0[8]; WD9 = WD_16_0[9]; WD10 = WD_16_0[10]; WD11 = WD_16_0[11]; WD12 = WD_16_0[12];
  //   WD13 = WD_16_0[13]; WD14 = WD_16_0[14]; WD15 = WD_16_0[15]; WD16 = WD_16_0[16]

  // Notes on the sheet:
  //   CLK: Hz: 2
endmodule
