// Digital circuit 4bit_prog_counter.dig as structural Verilog
module _4bit_prog_counter (
  input  [3:0] I_3_0,
  input  clk,
  output [3:0] O_3_0
);

  _4bit_reg _4bit_reg_1 (.din_3_0(I_3_0), .sel(1'b1), .clk(clk), .dout_3_0(O_3_0));

  // Other names for the same wires on the sheet: in[3:0] = I_3_0

  // Notes on the sheet:
  //   clk: Hz: 2
endmodule
