// Digital circuit 4bit_reg.dig as structural Verilog
module _4bit_reg (
  input  [3:0] din_3_0,
  input  sel,
  input  clk,
  output [3:0] dout_3_0
);

  _1bit_reg _1bit_reg_1 (.din(din_3_0[3]), .sel(sel), .clk(clk), .dout(dout_3_0[3]));
  _1bit_reg _1bit_reg_2 (.din(din_3_0[2]), .sel(sel), .clk(clk), .dout(dout_3_0[2]));
  _1bit_reg _1bit_reg_3 (.din(din_3_0[1]), .sel(sel), .clk(clk), .dout(dout_3_0[1]));
  _1bit_reg _1bit_reg_4 (.din(din_3_0[0]), .sel(sel), .clk(clk), .dout(dout_3_0[0]));

  // Other names for the same wires on the sheet: b0 = dout_3_0[0]; b1 = dout_3_0[1]; b2 = dout_3_0[2];
  //   b3 = dout_3_0[3]; a0 = din_3_0[0]; a1 = din_3_0[1]; a2 = din_3_0[2]; a3 = din_3_0[3]

  // Notes on the sheet:
  //   clk: Hz: 2
endmodule
