// Digital circuit 5bit_ALU.dig as structural Verilog
module _5bit_ALU (
  input  [4:0] B_4_0,
  input  [4:0] A_4_0,
  input  [1:0] OP_1_0,
  output [4:0] R_4_0
);

  wire [4:0] _5bit_adder_new_1_s_4_0, _5bit_and_1_p3, _5bit_shl_1_p3;

  // _5bit_and _5bit_and_1: pin names not known; wires that end beside it: B_4_0, A_4_0, _5bit_and_1_p3
  _5bit_adder_new _5bit_adder_new_1 (.X_4_0(A_4_0), .Y_4_0(B_4_0), .S_4_0(_5bit_adder_new_1_s_4_0));  // open: Cout
  // _5bit_shl _5bit_shl_1: pin names not known; wires that end beside it: A_4_0, B_4_0, _5bit_shl_1_p3
  Multiplexer #(.Selector_Bits(2), .Bits(5)) multiplexer_1 (
    .sel(OP_1_0), .in_0(_5bit_and_1_p3), .in_1(_5bit_adder_new_1_s_4_0), .in_2(_5bit_shl_1_p3),
    .in_3({5{1'b0}}), .out(R_4_0));

  // Other names for the same wires on the sheet: a[4:0] = A_4_0; b[4:0] = B_4_0
endmodule
