// Digital circuit 5bit_CU.dig as structural Verilog
module _5bit_CU (
  input  [3:0] opCode_3_0,
  input  ZF,
  output [1:0] OP_1_0,
  output RegEn,
  output immSel,
  output jmpSel
);

  wire and_1_out, and_3_out, and_4_out, and_5_out, or_2_out;

  and and_1 (and_1_out, ~opCode_3_0[2], ~opCode_3_0[3]);  // And
  and and_2 (immSel, opCode_3_0[2], ~opCode_3_0[3]);  // And
  and and_3 (and_3_out, ~opCode_3_0[2], opCode_3_0[3]);  // And
  and and_4 (and_4_out, ~opCode_3_0[0], ~opCode_3_0[1]);  // And
  and and_5 (and_5_out, opCode_3_0[0], ~opCode_3_0[1], ZF);  // And
  or or_1 (RegEn, and_1_out, immSel);
  or or_2 (or_2_out, and_4_out, and_5_out);
  and and_6 (jmpSel, and_3_out, or_2_out);

  assign OP_1_0 = opCode_3_0[1:0];
endmodule
