// Digital circuit 5bit_adder.dig as structural Verilog
module _5bit_adder (
  input  [4:0] a_4_0,
  input  [4:0] b_4_0,
  output [4:0] S_4_0,
  output Cout
);

  wire _2bit_adder_1_p1, _2bit_adder_2_p1, _2bit_adder_3_p1, _2bit_adder_4_p1;

  // _2bit_adder _2bit_adder_1: pin names not known; wires that end beside it: _2bit_adder_1_p1, b_4_0[4], Cout, a_4_0[4], S_4_0[4]
  // _2bit_adder _2bit_adder_2: pin names not known; wires that end beside it: _2bit_adder_2_p1, b_4_0[3], _2bit_adder_1_p1, a_4_0[3], S_4_0[3]
  // _2bit_adder _2bit_adder_3: pin names not known; wires that end beside it: _2bit_adder_3_p1, b_4_0[2], _2bit_adder_2_p1, a_4_0[2], S_4_0[2]
  // _2bit_adder _2bit_adder_4: pin names not known; wires that end beside it: _2bit_adder_4_p1, b_4_0[1], _2bit_adder_3_p1, a_4_0[1], S_4_0[1]
  // _2bit_adder _2bit_adder_5: pin names not known; wires that end beside it: 1'b0, b_4_0[0], _2bit_adder_4_p1, a_4_0[0], S_4_0[0]
endmodule
