// Digital circuit 5bit_adder_new.dig as structural Verilog
module _5bit_adder_new (
  input  [4:0] X_4_0,
  input  [4:0] Y_4_0,
  output [4:0] S_4_0,
  output Cout
);

  wire _1bit_adder_2_cout, _1bit_adder_3_cout, _1bit_adder_4_cout, _1bit_adder_5_cout;

  _1bit_adder _1bit_adder_1 (.X(X_4_0[4]), .Y(Y_4_0[4]), .cin(_1bit_adder_2_cout), .S(S_4_0[4]), .Cout(Cout));
  _1bit_adder _1bit_adder_2 (
    .X(X_4_0[3]), .Y(Y_4_0[3]), .cin(_1bit_adder_3_cout), .S(S_4_0[3]), .Cout(_1bit_adder_2_cout));
  _1bit_adder _1bit_adder_3 (
    .X(X_4_0[2]), .Y(Y_4_0[2]), .cin(_1bit_adder_4_cout), .S(S_4_0[2]), .Cout(_1bit_adder_3_cout));
  _1bit_adder _1bit_adder_4 (
    .X(X_4_0[1]), .Y(Y_4_0[1]), .cin(_1bit_adder_5_cout), .S(S_4_0[1]), .Cout(_1bit_adder_4_cout));
  _1bit_adder _1bit_adder_5 (.X(X_4_0[0]), .Y(Y_4_0[0]), .cin(1'b0), .S(S_4_0[0]), .Cout(_1bit_adder_5_cout));
endmodule
