// Digital circuit 5bit_and.dig as structural Verilog
module _5bit_and (
  input  [5:0] b_4_0,
  input  [4:0] a_4_0,
  output [5:0] O_4_0
);

  and and_1 (O_4_0[0], a_4_0[0], b_4_0[0]);
  and and_2 (O_4_0[1], a_4_0[1], b_4_0[1]);
  and and_3 (O_4_0[2], a_4_0[2], b_4_0[2]);
  and and_4 (O_4_0[3], a_4_0[3], b_4_0[3]);
  and and_5 (O_4_0[4], a_4_0[4], b_4_0[4]);
  // Pins of 5 and 6 bits meet at b_4_0
  // Pins of 5 and 6 bits meet at O_4_0
endmodule
