// Digital circuit 5bit_reg.dig as structural Verilog
module _5bit_reg (
  input  [4:0] din_4_0,
  input  sel,
  input  clk,
  output [4:0] dout_4_0
);

  _1bit_reg _1bit_reg_1 (.din(din_4_0[4]), .sel(sel), .clk(clk), .dout(dout_4_0[4]));
  _1bit_reg _1bit_reg_2 (.din(din_4_0[3]), .sel(sel), .clk(clk), .dout(dout_4_0[3]));
  _1bit_reg _1bit_reg_3 (.din(din_4_0[2]), .sel(sel), .clk(clk), .dout(dout_4_0[2]));
  _1bit_reg _1bit_reg_4 (.din(din_4_0[1]), .sel(sel), .clk(clk), .dout(dout_4_0[1]));
  _1bit_reg _1bit_reg_5 (.din(din_4_0[0]), .sel(sel), .clk(clk), .dout(dout_4_0[0]));

  // Other names for the same wires on the sheet: b0 = dout_4_0[0]; b1 = dout_4_0[1]; b2 = dout_4_0[2];
  //   b3 = dout_4_0[3]; b4 = dout_4_0[4]; a0 = din_4_0[0]; a1 = din_4_0[1]; a2 = din_4_0[2]; a3 = din_4_0[3];
  //   a4 = din_4_0[4]

  // Notes on the sheet:
  //   clk: Hz: 2
endmodule
