// Digital circuit 5bit_reg_set.dig as structural Verilog
module _5bit_reg_set (
  input  [2:0] wr_2_0,
  input  [4:0] wrd_4_0,
  input  [2:0] RA_2_0,
  input  [2:0] RB_2_0,
  input  WE,
  input  CLK,
  output [4:0] A_4_0,
  output [4:0] B_4_0
);

  wire a0, a1, a2, a3, a4, a5, d0, d1, d2, d3, d4, d5;
  wire [4:0] r0, r1, r2, r3, r4, r5;

  and and_1 (d0, a0, WE);
  and and_2 (d1, a1, WE);
  and and_3 (d2, a2, WE);
  Decoder #(.Selector_Bits(4)) decoder_1 (
    .out_0(a0), .out_1(a1), .out_2(a2), .out_3(a3), .out_4(a4), .out_5(a5));  // open: sel, out_6, out_7, out_8, out_9, out_10, out_11, out_12, out_13, out_14, out_15
  and and_4 (d3, a3, WE);
  and and_5 (d4, a4, WE);
  and and_6 (d5, a5, WE);
  _5bit_reg _5bit_reg_1 (.din_4_0(wrd_4_0), .sel(d5), .clk(CLK), .dout_4_0(r5));
  _5bit_reg _5bit_reg_2 (.din_4_0(wrd_4_0), .sel(d4), .clk(CLK), .dout_4_0(r4));
  _5bit_reg _5bit_reg_3 (.din_4_0(wrd_4_0), .sel(d3), .clk(CLK), .dout_4_0(r3));
  _5bit_reg _5bit_reg_4 (.din_4_0(wrd_4_0), .sel(d2), .clk(CLK), .dout_4_0(r2));
  _5bit_reg _5bit_reg_5 (.din_4_0(wrd_4_0), .sel(d1), .clk(CLK), .dout_4_0(r1));
  _5bit_reg _5bit_reg_6 (.din_4_0(wrd_4_0), .sel(d0), .clk(CLK), .dout_4_0(r0));
  Multiplexer #(.Selector_Bits(3), .Bits(5)) multiplexer_1 (
    .sel(RA_2_0), .in_0(r0), .in_1(r1), .in_2(r2), .in_3(r3), .in_4(r4), .in_5(r5), .in_6({5{1'b0}}),
    .in_7({5{1'b0}}), .out(A_4_0));
  Multiplexer #(.Selector_Bits(3), .Bits(5)) multiplexer_2 (
    .sel(RB_2_0), .in_0(r0), .in_1(r1), .in_2(r2), .in_3(r3), .in_4(r4), .in_5(r5), .in_6({5{1'b0}}),
    .in_7({5{1'b0}}), .out(B_4_0));
  // Pins of 5 and 6 bits meet at {6{1'b0}}

  // Notes on the sheet:
  //   CLK: Hz: 2
endmodule
