// Digital circuit 5bit_shl.dig as structural Verilog
module _5bit_shl (
  input  [4:0] a_4_0,
  input  [2:0] b_2_0,
  output [4:0] O_4_0
);

  Multiplexer #(.Selector_Bits(3)) multiplexer_1 (
    .sel(b_2_0), .in_0(a_4_0[4]), .in_1(a_4_0[3]), .in_2(a_4_0[2]), .in_3(a_4_0[1]), .in_4(a_4_0[0]),
    .in_5(1'b0), .in_6(1'b0), .in_7(1'b0), .out(O_4_0[4]));
  Multiplexer #(.Selector_Bits(3)) multiplexer_2 (
    .sel(b_2_0), .in_0(a_4_0[3]), .in_1(a_4_0[2]), .in_2(a_4_0[1]), .in_3(a_4_0[0]), .in_4(1'b0),
    .in_5(1'b0), .in_6(1'b0), .in_7(1'b0), .out(O_4_0[3]));
  Multiplexer #(.Selector_Bits(3)) multiplexer_3 (
    .sel(b_2_0), .in_0(a_4_0[2]), .in_1(a_4_0[1]), .in_2(a_4_0[0]), .in_3(1'b0), .in_4(1'b0), .in_5(1'b0),
    .in_6(1'b0), .in_7(1'b0), .out(O_4_0[2]));
  Multiplexer #(.Selector_Bits(3)) multiplexer_4 (
    .sel(b_2_0), .in_0(a_4_0[1]), .in_1(a_4_0[0]), .in_2(1'b0), .in_3(1'b0), .in_4(1'b0), .in_5(1'b0),
    .in_6(1'b0), .in_7(1'b0), .out(O_4_0[1]));
  Multiplexer #(.Selector_Bits(3)) multiplexer_5 (
    .sel(b_2_0), .in_0(a_4_0[0]), .in_1(1'b0), .in_2(1'b0), .in_3(1'b0), .in_4(1'b0), .in_5(1'b0),
    .in_6(1'b0), .in_7(1'b0), .out(O_4_0[0]));

  // Other names for the same wires on the sheet: a0 = a_4_0[0]; a1 = a_4_0[1]; a2 = a_4_0[2]; a3 = a_4_0[3];
  //   a4 = a_4_0[4]; sel[2:0] = b_2_0
endmodule
