// Digital circuit CPU.dig as structural Verilog
module CPU (
  input  WE,
  input  [16:0] WRD_16_0,
  input  CLK,
  input  [3:0] WR_3_0,
  input  PC_EN,
  input  [3:0] RA2_3_0,
  output [16:0] RD2_16_0,
  output [4:0] R_4_0,
  output [16:0] RD1_16_0
);

  wire cpu_clk, Imm_Sel, Jmp_Sel, Reg_En, ZF;
  wire [1:0] OP;
  wire [3:0] _4bit_pc__adder_1_o_3_0, _4bit_prog_counter_1_o_3_0, multiplexer_1_out;
  wire [4:0] _5bit_reg_set_1_a_4_0, _5bit_reg_set_1_b_4_0, multiplexer_2_out;
  wire [4:3] R2;

  Multiplexer #(.Bits(4)) multiplexer_1 (
    .sel(Jmp_Sel), .in_0(_4bit_pc__adder_1_o_3_0), .in_1(RD1_16_0[12:9]), .out(multiplexer_1_out));
  _4bit_prog_counter _4bit_prog_counter_1 (
    .I_3_0(multiplexer_1_out), .clk(cpu_clk), .O_3_0(_4bit_prog_counter_1_o_3_0));
  and and_1 (cpu_clk, CLK, PC_EN);
  _4bit_pc__adder _4bit_pc__adder_1 (.I_3_0(_4bit_prog_counter_1_o_3_0), .O_3_0(_4bit_pc__adder_1_o_3_0));
  _9x17_ram _9x17_ram_1 (
    .RA1_3_0(_4bit_prog_counter_1_o_3_0), .RA2_3_0(RA2_3_0), .WR_3_0(WR_3_0), .WE(WE), .WRD_16_0(WRD_16_0),
    .CLK(CLK), .RD2_16_0(RD2_16_0), .RD1_16_0(RD1_16_0));
  _5bit_CU _5bit_cu_1 (
    .opCode_3_0(RD1_16_0[16:13]), .ZF(ZF), .OP_1_0(OP), .RegEn(Reg_En), .immSel(Imm_Sel), .jmpSel(Jmp_Sel));
  _5bit_ALU _5bit_alu_1 (.A_4_0(_5bit_reg_set_1_a_4_0), .B_4_0(multiplexer_2_out), .R_4_0(R_4_0), .OP_1_0(OP));
  _5bit_reg_set _5bit_reg_set_1 (
    .wrd_4_0(R_4_0), .wr_2_0(RD1_16_0[12:10]), .WE(Reg_En), .CLK(cpu_clk), .RA_2_0(RD1_16_0[12:10]),
    .RB_2_0(RD1_16_0[9:7]), .A_4_0(_5bit_reg_set_1_a_4_0), .B_4_0(_5bit_reg_set_1_b_4_0));
  Multiplexer #(.Bits(5)) multiplexer_2 (
    .sel(Imm_Sel), .in_0(_5bit_reg_set_1_b_4_0), .in_1({R2, RD1_16_0[9:7]}), .out(multiplexer_2_out));
  // Pins of 3 and 5 bits meet at {R2, RD1_16_0[9:7]}

  // Other names for the same wires on the sheet: dont_care[6:0] = RD1_16_0[6:0]; R2[2:0] = RD1_16_0[9:7];
  //   Jmp_Addr[3:0] = RD1_16_0[12:9]; R1[2:0] = RD1_16_0[12:10]; OPcode[3:0] = RD1_16_0[16:13]

  // Notes on the sheet:
  //   CLK: Hz: 2
endmodule
